# Fritzing sketch 5v-3.3v-power-circuit (saved by Fritzing 0.9.1b)
breadboards: 1

parts:
  IC1 = Voltage Regulator [package=to-220-alt]
  U1 = V_REG_LD1117VXX [package=78xxl]
  C1 = Capacitor Polarized [package=cpol-radial-10uf-25v]
  C2 = Capacitor Polarized [package=cpol-radial-10uf-25v]
  J1 = Power Jack [package=power_jack_pth_lock]

nets:
  N1: IC1.GND, C1.+, J1.PWR
  GND: IC1.IN, U1.GND, C1.-, C2.-, J1.GND
  N2: IC1.OUT, U1.IN, C2.+

notes:
  5V Reg: Vin, gnd, output
  3.3V Reg: gnd, vout, vin
  Power Circuit: 5V and 3.3V for Aruduino and XBee/ESP8266
