# Fritzing sketch esp-perfboard (saved by Fritzing 0.9.1b)

parts:
  Part1 = Arduino Pro Mini v13
  Part2 = Arduino Pro Mini v13
  Microchip_EEPROM_24LC256-I/P1 = IC, DIP package, 8 pins [chip_label=IC]
  Part3 = Logic Level Converter
  U1 = ESP8266 WiFi Module [part_number=ESP8266]
  IC2 = Voltage Regulator [package=to-220-alt]
  U2 = V_REG_LD1117VXX [package=78xxl]
  C3 = Capacitor Polarized [package=cpol-radial-10uf-25v]
  C4 = Capacitor Polarized [package=cpol-radial-10uf-25v]
  J2 = Power Jack [package=power_jack_pth_lock]
  SJ1 = Solder Jumper [package=sj_2s-notrace]
  SJ2 = Solder Jumper [package=sj_2s-notrace]

nets:
  GND: Part1.GND, Part2.GND, Microchip_EEPROM_24LC256-I/P1.pin1, Microchip_EEPROM_24LC256-I/P1.pin4, Part3.GND, U1.GND, IC2.IN, U2.GND, C3.+, C4.+, J2.GND
  VCC: Part1.VCC, Part2.VCC, Microchip_EEPROM_24LC256-I/P1.pin8, Part3.HV, IC2.OUT, U2.IN, C4.-
  N1: Part1.RESET, Part2.D9_PWM
  N2: Part1.D1/RX, SJ2.2
  N3: Part1.D0/TX, SJ1.2
  N4: Part2.A4, Microchip_EEPROM_24LC256-I/P1.pin5
  N5: Part2.A5, Microchip_EEPROM_24LC256-I/P1.pin6
  N6: Part2.D8, Part3.TX_HV
  N7: Part2.D7, Part3.RX_HV
  N8: Part2.D1/RX, SJ1.1
  N9: Part2.D0/TX, SJ2.1
  N10: Part3.LV, U1.VCC, U1.CH_PD, U2.OUT
  N11: Part3.RX_LV, U1.RXD
  N12: Part3.TX_LV, U1.TXD
  N13: IC2.GND, C3.-, J2.PWR

notes:
  3.3V gnd, vout, vin
  5V Input, gnd, output
  100uF across input and ground. 10uF across 5V and ground

custom parts:
  ESP8266 WiFi Module: Generic WiFi Module based on the ESP8266 with onboard PCB antenna and UART communications
