# Fritzing sketch esp8266-arduino-voltage-divider (saved by Fritzing 0.9.1b)
breadboards: 1

parts:
  U1 = ESP8266 WiFi Module [part_number=ESP8266]
  Part3 = Arduino Uno (Rev3)
  R1 = Resistor [tolerance=±5% resistance=1k package=THT]
  R2 = Resistor [tolerance=±5% resistance=1k package=THT]
  R3 = Resistor [tolerance=±5% resistance=1k package=THT]

nets:
  N1: U1.RXD, R1.Pin_0, R3.Pin_0
  VCC: U1.VCC, U1.CH_PD, Part3.3V3
  GND: U1.GND, Part3.GND, R2.Pin_1
  N2: U1.TXD, Part3.D8
  N3: Part3.D7, R1.Pin_1
  N4: R2.Pin_0, R3.Pin_1

notes:
  SoftSerial RX 8, TX 7
  Voltage divider resistors are 1K

custom parts:
  ESP8266 WiFi Module: Generic WiFi Module based on the ESP8266 with onboard PCB antenna and UART communications
