# Fritzing sketch esp8266-arduino (saved by Fritzing 0.9.1b)
breadboards: 1

parts:
  U1 = ESP8266 WiFi Module [part_number=ESP8266]
  Part1 = Logic Level Converter
  Part3 = Arduino Uno (Rev3)

nets:
  N1: U1.RXD, Part1.RX_LV
  VCC: U1.VCC, U1.CH_PD, Part1.LV, Part3.3V3
  GND: U1.GND, Part1.GND, Part3.GND
  N2: U1.TXD, Part1.TX_LV
  N3: Part1.TX_HV, Part3.D8
  N4: Part1.RX_HV, Part3.D7
  N5: Part1.HV, Part3.5V

notes:
  SoftSerial RX 8, TX 7

custom parts:
  ESP8266 WiFi Module: Generic WiFi Module based on the ESP8266 with onboard PCB antenna and UART communications
