# Fritzing sketch esp8266-ftdi (saved by Fritzing 0.9.1b)

parts:
  Part1 = FTDI Basic Programmer
  U1 = ESP8266 WiFi Module [part_number=ESP8266]

nets:
  N1: Part1.RXI, U1.TXD
  N2: Part1.TXO, U1.RXD
  N3: Part1.POWER, U1.VCC, U1.CH_PD
  GND: Part1.GND, U1.GND

notes:
  3.3V

custom parts:
  ESP8266 WiFi Module: Generic WiFi Module based on the ESP8266 with onboard PCB antenna and UART communications
