# Fritzing sketch prototype-wiring (saved by Fritzing 0.9.1b)
breadboards: 1

parts:
  Part1 = Arduino Uno (Rev3)
  Part2 = Arduino Leonardo (Rev3b)
  Microchip_EEPROM_24LC256-I/P = IC, DIP package, 8 pins [chip_label=IC]
  U1 = XBee

nets:
  N1: Part1.D0/RX, Part2.D1/TX
  N2: Part1.D1/TX, Part2.D0/RX
  N3: Part1.RESET, Part2.D9_PWM/A9
  5V: Part1.5V, Part2.5V, Microchip_EEPROM_24LC256-I/P.pin8
  GND: Part1.GND, Part2.GND, Microchip_EEPROM_24LC256-I/P.pin1, Microchip_EEPROM_24LC256-I/P.pin2, Microchip_EEPROM_24LC256-I/P.pin3, Microchip_EEPROM_24LC256-I/P.pin4, U1.GND
  N4: Part2.D2/SDA, Microchip_EEPROM_24LC256-I/P.pin5
  N5: Part2.D3_PWM/SCL, Microchip_EEPROM_24LC256-I/P.pin6
  N6: Part2.D7, U1.pin3
  3V3: Part2.3V3, U1.VCC
  N7: Part2.D8/A8, U1.pin2

notes:
  programmer
  Microchip EEPROM (24LC256-I/P)
  application
  XBee Pins (pin 1 top left)
  1 - VCC
  2 - TX -> Arduino 8
  3 - RX -> Arduino 7
  10 - GND
